# Fritzing sketch AlternateControllerDiagram (saved by Fritzing 1.0.7)
breadboards: 2

parts:
  Part1 = Arduino Leonardo (Rev3b)
  S1 = Pushbutton [package="[THT]"]
  S2 = Pushbutton [package="[THT]"]
  S3 = Pushbutton [package="[THT]"]
  S4 = Pushbutton [package="[THT]"]
  R1 = Resistor [tolerance=±5% power=0.25W resistance=560 package=THT]
  HC-SR04_Sensor_1 = HC-SR04 Ultrasonic Distance Sensor
  LED1 = Super Flux RGB LED (com. anode)
  R2 = Resistor [tolerance=±5% power=0.25W resistance=560 package=THT]

nets:
  N1: Part1.D2/SDA, S2.Pin_3
  N2: Part1.D3_PWM/SCL, HC-SR04_Sensor_1.ECHO
  N3: Part1.D4/A6, S4.Pin_3
  N4: Part1.D5_PWM, HC-SR04_Sensor_1.TRIG
  N5: Part1.D7, S3.Pin_3
  5V: Part1.5V, HC-SR04_Sensor_1.VCC, LED1.red_cathode, LED1.blue_cathode, LED1.common_anode, R2.Pin_1
  N6: Part1.D8/A8, S1.Pin_3
  N7: Part1.D10_PWM/A10, R1.Pin_1
  N8: Part1.D11_PWM, R2.Pin_0
  GND: Part1.GND, S1.Pin_1, S1.Pin_2, S2.Pin_1, S2.Pin_2, S3.Pin_1, S3.Pin_2, S4.Pin_1, S4.Pin_2, HC-SR04_Sensor_1.GND
  N9: R1.Pin_0, LED1.green_cathode

notes:
  The RGB Piranha that I use has a different order of pins than the part fritzing has. Hence the wires are messy near the RGB to fix the discrepancy.
